// Logisim project EP01.circ as structural Verilog: 5 circuits, main circuit fullbitAdder
module fullbitAdder (
  input  cin,
  input  a0,
  input  b0,
  output s0,
  output cout
);

  wire and_1_out, and_2_out, xor_1_out;

  xor xor_1 (xor_1_out, a0, b0);
  and and_1 (and_1_out, a0, b0);
  xor xor_2 (s0, cin, xor_1_out);
  and and_2 (and_2_out, cin, xor_1_out);
  or or_1 (cout, and_2_out, and_1_out);
endmodule

module _4bitAdder (
  input  cin,
  input  in_2,
  input  in_3,
  input  in_4,
  input  in_5,
  input  in_6,
  input  in_7,
  input  in_8,
  input  in_9,
  output out_10,
  output out_11,
  output out_12,
  output out_13,
  output over
);

  wire fullbitadder_1_cout, fullbitadder_2_cout, fullbitadder_3_cout;

  fullbitAdder fullbitadder_1 (.cin(cin), .a0(in_2), .b0(in_6), .s0(out_10), .cout(fullbitadder_1_cout));
  fullbitAdder fullbitadder_2 (
    .cin(fullbitadder_1_cout), .a0(in_3), .b0(in_7), .s0(out_11), .cout(fullbitadder_2_cout));
  fullbitAdder fullbitadder_3 (
    .cin(fullbitadder_2_cout), .a0(in_4), .b0(in_8), .s0(out_12), .cout(fullbitadder_3_cout));
  fullbitAdder fullbitadder_4 (.cin(fullbitadder_3_cout), .a0(in_5), .b0(in_9), .s0(out_13), .cout(over));
endmodule

module Full_Adder (
  input  A0,
  input  Ci,
  input  A1,
  input  A2,
  input  A3,
  input  B0,
  input  B1,
  input  B2,
  input  B3,
  output S0,
  output S1,
  output S2,
  output S3,
  output Overflow
);

  wire decoder_1_out_5, decoder_1_out_6, decoder_1_out_7, decoder_1_out_8, decoder_1_out_9, decoder_1_out_10,
       decoder_1_out_11, decoder_1_out_12, decoder_2_out_5, decoder_2_out_6, decoder_2_out_7,
       decoder_2_out_8, decoder_2_out_9, decoder_2_out_10, decoder_2_out_11, decoder_2_out_12,
       decoder_3_out_5, decoder_3_out_6, decoder_3_out_7, decoder_3_out_8, decoder_3_out_9, decoder_3_out_10,
       decoder_3_out_11, decoder_3_out_12;

  Decoder decoder_1 (
    .in_1(A0), .in_2(A1), .in_3(A2), .in_4(A3), .out_5(decoder_1_out_5), .out_6(decoder_1_out_6),
    .out_7(decoder_1_out_7), .out_8(decoder_1_out_8), .out_9(decoder_1_out_9), .out_10(decoder_1_out_10),
    .out_11(decoder_1_out_11), .out_12(decoder_1_out_12));
  Decoder decoder_2 (
    .in_1(B0), .in_2(B1), .in_3(B2), .in_4(B3), .out_5(decoder_2_out_5), .out_6(decoder_2_out_6),
    .out_7(decoder_2_out_7), .out_8(decoder_2_out_8), .out_9(decoder_2_out_9), .out_10(decoder_2_out_10),
    .out_11(decoder_2_out_11), .out_12(decoder_2_out_12));
  _4bitAdder u_4bitadder_1 (
    .cin(Ci), .in_2(A0), .in_3(A1), .in_4(A2), .in_5(A3), .in_6(B0), .in_7(B1), .in_8(B2), .in_9(B3),
    .out_10(S0), .out_11(S1), .out_12(S2), .out_13(S3), .over(Overflow));
  _7_Segment_Display u_7_segment_display_1 (
    .g(decoder_1_out_5), .f(decoder_1_out_6), .a(decoder_1_out_7), .b(decoder_1_out_8), .e(decoder_1_out_9),
    .d(decoder_1_out_10), .c(decoder_1_out_11), .dp(decoder_1_out_12));
  _7_Segment_Display u_7_segment_display_2 (
    .g(decoder_2_out_5), .f(decoder_2_out_6), .a(decoder_2_out_7), .b(decoder_2_out_8), .e(decoder_2_out_9),
    .d(decoder_2_out_10), .c(decoder_2_out_11), .dp(decoder_2_out_12));
  Decoder decoder_3 (
    .in_1(S0), .in_2(S1), .in_3(S2), .in_4(S3), .out_5(decoder_3_out_5), .out_6(decoder_3_out_6),
    .out_7(decoder_3_out_7), .out_8(decoder_3_out_8), .out_9(decoder_3_out_9), .out_10(decoder_3_out_10),
    .out_11(decoder_3_out_11), .out_12(decoder_3_out_12));
  _7_Segment_Display u_7_segment_display_3 (
    .g(decoder_3_out_5), .f(decoder_3_out_6), .a(decoder_3_out_7), .b(decoder_3_out_8), .e(decoder_3_out_9),
    .d(decoder_3_out_10), .c(decoder_3_out_11), .dp(decoder_3_out_12));
endmodule

module Decoder (
  input  in_1,
  input  in_2,
  input  in_3,
  input  in_4,
  output out_5,
  output out_6,
  output out_7,
  output out_8,
  output out_9,
  output out_10,
  output out_11,
  output out_12
);

  Multiplexer #(.select(4), .width(8), .enable("false")) multiplexer_1 (
    .in0(8'h7e), .in1(8'h48), .in2(8'h3d), .in3(8'h6d), .in4(8'h4b), .in5(8'h67), .in6(8'h77), .in7(8'h4c),
    .in8(8'h7f), .in9(8'h4f), .in10(8'h5f), .in11(8'h73), .in12(8'h36), .in13(8'h79), .in14(8'h37),
    .in15(8'h17), .out({out_12, out_11, out_10, out_9, out_8, out_7, out_6, out_5}),
    .sel({in_4, in_3, in_2, in_1}));
  _7_Segment_Display u_7_segment_display_1 (
    .g(out_5), .f(out_6), .a(out_7), .b(out_8), .e(out_9), .d(out_10), .c(out_11), .dp(out_12));
endmodule

module TTL (
);

  _747266 u_747266_1 ();  // open: pin1, pin2, pin3, pin4, pin5, pin6, pin13, pin12, pin11, pin10, pin9, pin8
  _7408 u_7408_1 ();  // open: pin1, pin2, pin3, pin4, pin5, pin6, pin13, pin12, pin11, pin10, pin9, pin8
  _7432 u_7432_1 ();  // open: pin1, pin2, pin3, pin4, pin5, pin6, pin13, pin12, pin11, pin10, pin9, pin8
endmodule
