// Logisim project EP02.circ as structural Verilog
module SomaCompleta (
  input  a,
  input  b,
  input  CIn,
  output S,
  output COut
);

  wire and_1_out, and_2_out, xor_1_out;

  xor xor_1 (xor_1_out, a, b);
  and and_1 (and_1_out, a, b);
  xor xor_2 (S, xor_1_out, CIn);
  and and_2 (and_2_out, xor_1_out, CIn);
  or or_1 (COut, and_2_out, and_1_out);
endmodule

module ULA (
  input  bitInvert,
  input  CIn,
  input  [1:0] Opcode,
  input  a,
  input  b,
  output Result,
  output COut
);

  wire and_1_out, multiplexer_1_out, not_1_out, not_2_out, or_1_out, somacompleta_1_s;

  Multiplexer #(.enable("false")) multiplexer_1 (.in0(b), .in1(not_1_out), .out(multiplexer_1_out), .sel(bitInvert));
  not not_1 (not_1_out, b);
  SomaCompleta somacompleta_1 (.a(a), .b(multiplexer_1_out), .CIn(CIn), .S(somacompleta_1_s), .COut(COut));
  and and_1 (and_1_out, a, b);
  or or_1 (or_1_out, a, b);
  not not_2 (not_2_out, a);
  Multiplexer #(.select(2), .enable("false")) multiplexer_2 (
    .in0(and_1_out), .in1(or_1_out), .in2(not_2_out), .in3(somacompleta_1_s), .out(Result), .sel(Opcode));
endmodule

module _4Bit_ULA (
  input  [3:0] b,
  input  [3:0] a,
  input  BInvert,
  input  [1:0] OpCode,
  output [3:0] S,
  output COut
);

  wire ula_1_cout, ula_2_cout, ula_3_cout;

  ULA ula_1 (.a(a[0]), .b(b[0]), .Result(S[0]), .bitInvert(BInvert), .CIn(BInvert), .Opcode(OpCode), .COut(ula_1_cout));
  ULA ula_2 (
    .a(a[1]), .b(b[1]), .Result(S[1]), .bitInvert(BInvert), .CIn(ula_1_cout), .Opcode(OpCode),
    .COut(ula_2_cout));
  ULA ula_3 (
    .a(a[2]), .b(b[2]), .Result(S[2]), .bitInvert(BInvert), .CIn(ula_2_cout), .Opcode(OpCode),
    .COut(ula_3_cout));
  ULA ula_4 (.a(a[3]), .b(b[3]), .Result(S[3]), .bitInvert(BInvert), .CIn(ula_3_cout), .Opcode(OpCode), .COut(COut));
endmodule
